# Fritzing sketch 20220822-01 (saved by Fritzing 0.9.10b)
breadboards: 1

parts:
  Mod1 = Raspberry Pi 4B
  DHT22 = Humidity and Temperature Sensor RHT03
  SW1 = DIP Switch 8 Position [package=dipswitch-08]
  100kΩ電阻 = Resistor [tolerance=±5% power=0.25 resistance=100000 package=THT]
  100kΩ電阻1 = Resistor [tolerance=±5% power=0.25 resistance=100000 package=THT]
  100kΩ電阻2 = Resistor [tolerance=±5% power=0.25 resistance=100000 package=THT]
  100kΩ電阻3 = Resistor [tolerance=±5% power=0.25 resistance=100000 package=THT]
  100kΩ電阻4 = Resistor [tolerance=±5% power=0.25 resistance=100000 package=THT]
  100kΩ電阻5 = Resistor [tolerance=±5% power=0.25 resistance=100000 package=THT]

nets:
  3V3: Mod1.3V3, DHT22.Vcc, SW1.13, SW1.14, SW1.15, SW1.16, 100kΩ電阻.Pin_0, 100kΩ電阻1.Pin_0
  N1: Mod1.GND, DHT22.GND_2, 100kΩ電阻2.Pin_1, 100kΩ電阻3.Pin_1, 100kΩ電阻4.Pin_1, 100kΩ電阻5.Pin_1
  N2: Mod1.GPIO17, DHT22.Data-signal, 100kΩ電阻.Pin_1, 100kΩ電阻1.Pin_1
  N3: Mod1.GPIO27, SW1.1, 100kΩ電阻2.Pin_0
  N4: Mod1.GPIO22, SW1.2, 100kΩ電阻3.Pin_0
  N5: Mod1.GPIO5, SW1.3, 100kΩ電阻4.Pin_0
  N6: Mod1.GPIO6, SW1.4, 100kΩ電阻5.Pin_0
