# Fritzing sketch 20230705-01-easyversion (saved by Fritzing 0.9.10b)
breadboards: 1

parts:
  Pi4 = Raspberry Pi 4B
  DHT22 = Humidity and Temperature Sensor RHT03
  Switch = DIP Switch 8 Position [package=dipswitch-08]
  100kΩ電阻 = Resistor [tolerance=±5% power=0.25 resistance=100000 package=THT]
  100kΩ電阻1 = Resistor [tolerance=±5% power=0.25 resistance=100000 package=THT]
  100kΩ電阻2 = Resistor [tolerance=±5% power=0.25 resistance=100000 package=THT]
  100kΩ電阻3 = Resistor [tolerance=±5% power=0.25 resistance=100000 package=THT]
  100kΩ電阻4 = Resistor [tolerance=±5% power=0.25 resistance=100000 package=THT]
  100kΩ電阻5 = Resistor [tolerance=±5% power=0.25 resistance=100000 package=THT]

nets:
  3V3: Pi4.3V3, DHT22.Vcc, Switch.13, Switch.14, Switch.15, Switch.16, 100kΩ電阻.Pin_0, 100kΩ電阻1.Pin_0
  N1: Pi4.GND, DHT22.GND_2, 100kΩ電阻2.Pin_1, 100kΩ電阻3.Pin_1, 100kΩ電阻4.Pin_1, 100kΩ電阻5.Pin_1
  N2: Pi4.GPIO17, DHT22.Data-signal, 100kΩ電阻.Pin_1, 100kΩ電阻1.Pin_1
  N3: Pi4.GPIO27, Switch.1, 100kΩ電阻2.Pin_0
  N4: Pi4.GPIO22, Switch.2, 100kΩ電阻3.Pin_0
  N5: Pi4.GPIO5, Switch.3, 100kΩ電阻4.Pin_0
  N6: Pi4.GPIO6, Switch.4, 100kΩ電阻5.Pin_0
